# Fritzing sketch wind-informer (saved by Fritzing 0.9.0b)
breadboards: 1

parts:
  Часть1 = Arduino Uno (Rev3)
  J1 = Screw terminal - 2 pins [package=THT]
  J2 = Screw terminal - 2 pins [package=THT]
  J3 = Screw terminal - 2 pins [package=THT]
  SP1 = SPEAKER [package=pcb_mount_speaker]
  R1 = Resistor [tolerance=±5% resistance=220 package="0603 [SMD]"]
  R2 = Resistor [tolerance=±5% resistance=220 package="0603 [SMD]"]
  Audio1 = DFPlayer Mini
  Meteo1 = Anemometer kit
  BAT1 = BC9VPC [package=bc9vpc]

nets:
  N1: Часть1.A0, J2.pin2, Meteo1.Signal
  N2: Часть1.D0/RX, R1.Pin_0
  N3: Часть1.D1/TX, R2.Pin_0
  3V3: Часть1.3V3, Audio1.VCC
  5V: Часть1.5V, J1.pin1, Meteo1.VCC
  GND: Часть1.GND, J1.pin2, Audio1.GND#6, Meteo1.GND, BAT1.V-
  N4: Часть1.VIN, BAT1.V+
  N5: J3.pin1, SP1.-, Audio1.SPK1
  N6: J3.pin2, SP1.+, Audio1.SPK2
  N7: R1.Pin_1, Audio1.TX
  N8: R2.Pin_1, Audio1.RX

custom parts:
  DFPlayer Mini: MP3 player module.
  Anemometer kit: Anemometer kit.
